// Logisim project Lab_1.circ as structural Verilog: 1 circuit, main circuit main
module main (
  input  in_1,
  input  in_2,
  input  in_3,
  input  in_4
);

  wire n74194_1_pin2, n74194_1_pin3, n74194_1_pin7, n74194_1_pin11, n74194_1_pin12, n74194_1_pin13,
       n74194_1_pin14, n74194_2_pin3, n74194_2_pin4, n74194_2_pin5, n74194_2_pin6, n74194_2_pin7,
       n74194_2_pin9, n74194_2_pin11, n74194_2_pin12, n74194_2_pin13, n74194_2_pin14, n74194_2_pin15,
       n74194_3_pin2, n74194_3_pin3, n74194_3_pin4, n74194_3_pin5, n74194_3_pin6, n74194_3_pin7,
       n74194_3_pin9, n74194_3_pin11, n74194_3_pin12, n74194_3_pin13, n74194_3_pin14, n74194_3_pin15;

  _74194 u_74194_1 (
    .pin1(in_1), .pin2(n74194_1_pin2), .pin3(n74194_1_pin3), .pin4(n74194_1_pin3), .pin5(n74194_1_pin3),
    .pin6(in_1), .pin7(n74194_1_pin7), .pin15(n74194_1_pin7), .pin14(n74194_1_pin14), .pin13(n74194_1_pin13),
    .pin12(n74194_1_pin12), .pin11(n74194_1_pin11), .pin10(in_1), .pin9(in_2));
  _74194 u_74194_2 (
    .pin1(in_3), .pin3(n74194_2_pin3), .pin4(n74194_2_pin4), .pin5(n74194_2_pin5), .pin6(n74194_2_pin6),
    .pin7(n74194_2_pin7), .pin15(n74194_2_pin15), .pin14(n74194_2_pin14), .pin13(n74194_2_pin13),
    .pin12(n74194_2_pin12), .pin11(n74194_2_pin11), .pin10(in_3), .pin9(n74194_2_pin9));  // open: pin2
  _74194 u_74194_3 (
    .pin1(in_4), .pin2(n74194_3_pin2), .pin3(n74194_3_pin3), .pin4(n74194_3_pin4), .pin5(n74194_3_pin5),
    .pin6(n74194_3_pin6), .pin7(n74194_3_pin7), .pin15(n74194_3_pin15), .pin14(n74194_3_pin14),
    .pin13(n74194_3_pin13), .pin12(n74194_3_pin12), .pin11(n74194_3_pin11), .pin10(in_4), .pin9(n74194_3_pin9));
  not not_1 (n74194_3_pin7, n74194_3_pin15);
  LED led_1 (.in(n74194_1_pin7));
  LED led_2 (.in(n74194_1_pin14));
  LED led_3 (.in(n74194_1_pin13));
  LED led_4 (.in(n74194_1_pin12));
  Clock clock_1 (.out(n74194_1_pin11));
  LED led_5 (.in(n74194_2_pin15));
  LED led_6 (.in(n74194_2_pin14));
  LED led_7 (.in(n74194_2_pin13));
  LED led_8 (.in(n74194_2_pin12));
  Clock clock_2 (.out(n74194_2_pin11));
  _7410 u_7410_1 (
    .pin3(n74194_2_pin12), .pin4(n74194_2_pin13), .pin5(n74194_2_pin14), .pin6(n74194_2_pin7));  // open: pin1, pin2, pin13, pin12, pin11, pin10, pin9, pin8
  LED led_9 (.in(n74194_3_pin15));
  LED led_10 (.in(n74194_3_pin14));
  LED led_11 (.in(n74194_3_pin13));
  LED led_12 (.in(n74194_3_pin12));
  Clock clock_3 (.out(n74194_3_pin11));
  // Digital_Oscilloscope digital_oscilloscope_1: pin names not known; wires that end beside it: 1'b1, n74194_1_pin11, n74194_1_pin7, n74194_1_pin14, n74194_1_pin13, n74194_1_pin12
  // Digital_Oscilloscope digital_oscilloscope_2: pin names not known; wires that end beside it: 1'b1, n74194_2_pin11, n74194_2_pin15, n74194_2_pin14, n74194_2_pin13, n74194_2_pin12
  // Digital_Oscilloscope digital_oscilloscope_3: pin names not known; wires that end beside it: 1'b1, n74194_3_pin11, n74194_3_pin15, n74194_3_pin14, n74194_3_pin13, n74194_3_pin12
  // also tied to GND on the sheet: {n74194_1_pin3, n74194_2_pin9, n74194_3_pin9}

  // Notes on the sheet:
  //   A
  //   B
  //   C
  //   D
  //   A
  //   B
  //   C
  //   D
  //   A
  //   B
  //   C
  //   D
endmodule
