// Logisim project Lab_2.circ as structural Verilog: 1 circuit, main circuit main
module main (
  input  A,
  input  B,
  input  C,
  input  D,
  input  A_2,
  input  B_2,
  input  C_2
);

  wire n74151_1_pin1, n74151_1_pin2, n74151_1_pin5, n74151_2_pin5, n74151_2_pin14, nand_1_out, nand_2_out,
       nand_3_out, nand_4_out, nand_5_out, nand_6_out, nand_7_out, nand_8_out, nand_9_out, nand_10_out,
       nand_11_out, nand_12_out, nand_13_out, nand_14_out, not_1_out;

  not not_1 (not_1_out, D);
  nand nand_1 (nand_1_out, A_2, A_2);
  nand nand_2 (nand_2_out, B_2, B_2);
  nand nand_3 (nand_3_out, C_2, C_2);
  _74151 #(.ShowInternalStructure("true")) u_74151_1 (
    .pin1(n74151_1_pin1), .pin2(n74151_1_pin2), .pin3(n74151_1_pin2), .pin4(n74151_1_pin2),
    .pin5(n74151_1_pin5), .pin15(n74151_1_pin1), .pin14(n74151_1_pin2), .pin13(n74151_1_pin2),
    .pin12(n74151_1_pin2), .pin11(A_2), .pin10(B_2), .pin9(C_2));  // open: pin6, pin7
  nand nand_4 (nand_4_out, A, A);
  nand nand_5 (nand_5_out, B, B);
  nand nand_6 (nand_6_out, C, C);
  nand nand_7 (nand_7_out, D, D);
  LED led_1 (.in(n74151_2_pin5));
  _74151 #(.ShowInternalStructure("true")) u_74151_2 (
    .pin1(not_1_out), .pin2(not_1_out), .pin3(not_1_out), .pin4(not_1_out), .pin5(n74151_2_pin5),
    .pin15(not_1_out), .pin14(n74151_2_pin14), .pin13(n74151_2_pin14), .pin12(n74151_2_pin14), .pin11(A),
    .pin10(B), .pin9(C));  // open: pin6, pin7
  nand nand_8 (nand_8_out, nand_2_out, nand_3_out);
  nand nand_9 (nand_9_out, nand_1_out, B_2);
  nand nand_10 (nand_10_out, A_2, C_2);
  LED led_2 (.in(n74151_1_pin5));
  nand nand_11 (nand_11_out, nand_8_out, nand_9_out, nand_10_out);
  LED led_3 (.in(nand_11_out));
  nand nand_12 (nand_12_out, nand_4_out, nand_5_out, nand_7_out);
  nand nand_13 (nand_13_out, nand_6_out, nand_7_out);
  nand nand_14 (nand_14_out, nand_12_out, nand_13_out);
  LED led_4 (.in(nand_14_out));
  // also tied to GND on the sheet: {n74151_1_pin1, n74151_2_pin14}
  // also tied to VCC on the sheet: n74151_1_pin2

  // Notes on the sheet:
  //   Part B
  //   Part A
endmodule
