// Logisim project Lab_3.circ as structural Verilog
module main (
  input  A,
  input  in_2,
  input  A_2,
  input  B,
  input  A_3,
  input  B_2,
  input  C,
  input  D,
  input  A_4,
  input  B_3,
  input  C_2,
  input  D_2
);

  wire and_1_out, and_2_out, and_3_out, and_4_out, clock_1_out, clock_2_out, d_ff_1_q, d_ff_2_q, d_ff_2_qn,
       d_ff_3_q, d_ff_3_qn, d_ff_4_q, d_ff_4_qn, digital_oscilloscope_1_p3, nand_1_out, nand_2_out,
       nand_3_out, nand_4_out, nand_5_out, nand_7_out, not_1_out, not_2_out, not_3_out, not_4_out, not_5_out,
       not_6_out, not_7_out, not_8_out, not_9_out, not_10_out, or_1_out, or_2_out;

  not not_1 (not_1_out, A);
  not not_2 (not_2_out, A_2);
  not not_3 (not_3_out, A_3);
  not not_4 (not_4_out, not_3_out);
  not not_5 (not_5_out, not_1_out);
  not not_6 (not_6_out, not_5_out);
  not not_7 (not_7_out, not_2_out);
  not not_8 (not_8_out, not_4_out);
  not not_9 (not_9_out, A_4);
  and and_1 (and_1_out, A, in_2);
  and and_2 (and_2_out, not_6_out, in_2);
  and and_3 (and_3_out, A_2, B);
  not not_10 (not_10_out, not_7_out);
  and and_4 (and_4_out, not_10_out, B);
  nand nand_1 (nand_1_out, not_8_out, B_2, D);
  nand nand_2 (nand_2_out, D, C, A_3);
  nand nand_3 (nand_3_out, not_9_out, B_3, D_2);
  nand nand_4 (nand_4_out, D_2, C_2, A_4);
  nand nand_5 (nand_5_out, B_3, C_2, D_2);
  or or_1 (or_1_out, and_1_out, and_2_out);
  Clock clock_1 (.out(clock_1_out));
  or or_2 (or_2_out, and_3_out, and_4_out);
  D_Flip_Flop d_ff_1 (.D(or_1_out), .clk(clock_1_out), .Q(d_ff_1_q));  // open: Qn, preset, reset
  D_Flip_Flop d_ff_2 (.D(d_ff_2_qn), .clk(or_2_out), .Q(d_ff_2_q), .Qn(d_ff_2_qn));  // open: preset, reset
  LED led_1 (.in(or_2_out));
  Clock clock_2 (.out(clock_2_out));
  // Digital_Oscilloscope digital_oscilloscope_1: pin names not known; wires that end beside it: clock_2_out, A_3, digital_oscilloscope_1_p3
  nand nand_6 (digital_oscilloscope_1_p3, nand_1_out, nand_2_out);
  LED led_2 (.in(digital_oscilloscope_1_p3));
  nand nand_7 (nand_7_out, nand_3_out, nand_4_out, nand_5_out);
  LED led_3 (.in(nand_7_out));
  LED led_4 (.in(d_ff_2_q));
  D_Flip_Flop d_ff_3 (
    .D(d_ff_3_qn), .clk(digital_oscilloscope_1_p3), .Q(d_ff_3_q), .Qn(d_ff_3_qn));  // open: preset, reset
  D_Flip_Flop d_ff_4 (.D(d_ff_4_qn), .clk(nand_7_out), .Q(d_ff_4_q), .Qn(d_ff_4_qn));  // open: preset, reset
  LED led_5 (.in(d_ff_3_q));
  LED led_6 (.in(d_ff_4_q));

  // Notes on the sheet:
  //   B
endmodule

// VHDL entity F, as the project stores it:
--------------------------------------------------------------------------------
-- Project :
-- File    :
-- Autor   :
-- Date    :
--
--------------------------------------------------------------------------------
-- Description :
--
--------------------------------------------------------------------------------

LIBRARY ieee;
USE ieee.std_logic_1164.all;

ENTITY F IS
  PORT (
  ------------------------------------------------------------------------------
  --Insert input ports below
    clock      : IN  std_logic;                    -- input bit example
    val        : IN  std_logic_vector(3 DOWNTO 0); -- input vector example
  ------------------------------------------------------------------------------
  --Insert output ports below
    max        : OUT std_logic;                    -- output bit example
    cpt        : OUT std_logic_vector(3 DOWNTO 0)  -- output vector example
    );
END F;

--------------------------------------------------------------------------------
--Complete your VHDL description below
--------------------------------------------------------------------------------

ARCHITECTURE TypeArchitecture OF F IS

BEGIN


END TypeArchitecture;
