// Logisim project Lab_4.circ as structural Verilog: 1 circuit, main circuit main
module main (
  input  in_1,
  input  in_2,
  input  in_3,
  input  in_4
);

  wire and_1_out, and_2_out, and_3_out, and_4_out, and_5_out, and_6_out, and_7_out, and_8_out, and_9_out,
       and_10_out, and_11_out, and_12_out, and_13_out, clock_1_out, clock_2_out, clock_3_out, clock_4_out,
       d_ff_1_q, d_ff_1_qn, d_ff_2_qn, j_k_ff_1_q, j_k_ff_1_qn, j_k_ff_2_q, j_k_ff_2_qn, j_k_ff_3_q,
       j_k_ff_3_qn, j_k_ff_4_q, j_k_ff_4_qn, j_k_ff_5_q, j_k_ff_5_qn, j_k_ff_6_q, j_k_ff_6_qn, nand_1_out,
       nand_2_out, nand_3_out, nand_4_out, nand_5_out, nand_6_out, nand_7_out, nand_8_out, nand_9_out,
       nand_10_out, nand_11_out, not_1_out, not_2_out, not_3_out, not_4_out, not_5_out, or_1_out, or_2_out,
       or_3_out;

  not not_1 (not_1_out, in_2);
  not not_2 (not_2_out, in_4);
  and and_1 (and_1_out, d_ff_1_qn, in_1);
  and and_2 (and_2_out, in_1, not_3_out);
  not not_3 (not_3_out, d_ff_2_qn);
  and and_3 (and_3_out, in_1, d_ff_1_q);
  and and_4 (and_4_out, j_k_ff_1_qn, in_2);
  and and_5 (and_5_out, not_1_out, j_k_ff_1_q);
  and and_6 (and_6_out, j_k_ff_2_qn, j_k_ff_1_q);
  and and_7 (and_7_out, in_2, j_k_ff_1_q, j_k_ff_2_qn);
  and and_8 (and_8_out, j_k_ff_2_q, not_1_out);
  nand nand_1 (nand_1_out, j_k_ff_3_qn, in_4);
  nand nand_2 (nand_2_out, not_2_out, j_k_ff_3_q);
  nand nand_3 (nand_3_out, j_k_ff_4_qn, j_k_ff_3_q);
  nand nand_4 (nand_4_out, in_4, j_k_ff_3_q, j_k_ff_4_qn);
  nand nand_5 (nand_5_out, j_k_ff_4_q, not_2_out);
  or or_1 (or_1_out, and_5_out, and_6_out);
  nand nand_6 (nand_6_out, nand_1_out, nand_1_out);
  nand nand_7 (nand_7_out, nand_4_out, nand_4_out);
  nand nand_8 (nand_8_out, nand_5_out, nand_5_out);
  nand nand_9 (nand_9_out, nand_2_out, nand_3_out);
  or or_2 (or_2_out, and_1_out, and_2_out);
  or or_3 (or_3_out, and_2_out, and_3_out);
  Clock clock_1 (.out(clock_1_out));
  D_Flip_Flop d_ff_1 (.D(or_2_out), .clk(clock_1_out), .Q(d_ff_1_q), .Qn(d_ff_1_qn));  // open: preset, reset
  D_Flip_Flop d_ff_2 (.D(or_3_out), .clk(clock_1_out), .Qn(d_ff_2_qn));  // open: Q, preset, reset
  J_K_Flip_Flop j_k_ff_1 (
    .J(and_4_out), .K(or_1_out), .clk(clock_2_out), .Q(j_k_ff_1_q), .Qn(j_k_ff_1_qn));  // open: preset, reset
  J_K_Flip_Flop j_k_ff_2 (
    .J(and_7_out), .K(and_8_out), .clk(clock_2_out), .Q(j_k_ff_2_q), .Qn(j_k_ff_2_qn));  // open: preset, reset
  Clock clock_2 (.out(clock_2_out));
  J_K_Flip_Flop j_k_ff_3 (
    .J(nand_6_out), .K(nand_9_out), .clk(clock_3_out), .Q(j_k_ff_3_q), .Qn(j_k_ff_3_qn));  // open: preset, reset
  J_K_Flip_Flop j_k_ff_4 (
    .J(nand_7_out), .K(nand_8_out), .clk(clock_3_out), .Q(j_k_ff_4_q), .Qn(j_k_ff_4_qn));  // open: preset, reset
  Clock clock_3 (.out(clock_3_out));
  LED led_1 (.in(d_ff_1_q));
  not not_4 (not_4_out, d_ff_2_qn);
  LED led_2 (.in(not_4_out));
  LED led_3 (.in(j_k_ff_1_q));
  LED led_4 (.in(j_k_ff_2_q));
  LED led_5 (.in(j_k_ff_3_q));
  LED led_6 (.in(j_k_ff_4_q));
  and and_9 (and_9_out, d_ff_1_q, not_4_out);
  and and_10 (and_10_out, j_k_ff_1_q, j_k_ff_2_q);
  LED led_7 (.in(and_10_out));
  nand nand_10 (nand_10_out, j_k_ff_3_q, j_k_ff_4_q);
  LED led_8 (.in(and_9_out));
  nand nand_11 (nand_11_out, nand_10_out, nand_10_out);
  LED led_9 (.in(nand_11_out));
  and and_11 (and_11_out, in_3, j_k_ff_6_q);
  not not_5 (not_5_out, and_11_out);
  and and_12 (and_12_out, j_k_ff_5_q, in_3);
  Clock clock_4 (.out(clock_4_out));
  J_K_Flip_Flop j_k_ff_5 (
    .J(in_3), .K(not_5_out), .clk(clock_4_out), .Q(j_k_ff_5_q), .Qn(j_k_ff_5_qn));  // open: preset, reset
  J_K_Flip_Flop j_k_ff_6 (
    .J(and_12_out), .K(not_5_out), .clk(clock_4_out), .Q(j_k_ff_6_q), .Qn(j_k_ff_6_qn));  // open: preset, reset
  LED led_10 (.in(j_k_ff_5_q));
  LED led_11 (.in(j_k_ff_6_q));
  and and_13 (and_13_out, j_k_ff_5_q, j_k_ff_6_q);
  LED led_12 (.in(and_13_out));

  // Notes on the sheet:
  //   y1
  //   y2
  //   y1
  //   y2
  //   y1
  //   y2
  //   Z
  //   Z
  //   Z
  //   y1
  //   y2
  //   Z
endmodule
