// Logisim project Lab_5.circ as structural Verilog: 1 circuit, main circuit main
module main (
  input  X,
  input  in_2,
  input  in_3
);

  wire and_1_out, and_2_out, and_3_out, and_4_out, clock_1_out, d_ff_1_q, d_ff_1_qn, j_k_ff_1_q, j_k_ff_1_qn,
       xor_1_out;

  xor xor_1 (xor_1_out, d_ff_1_q, X);
  Clock clock_1 (.out(clock_1_out));
  D_Flip_Flop d_ff_1 (.D(xor_1_out), .clk(clock_1_out), .Q(d_ff_1_q), .Qn(d_ff_1_qn), .reset(in_2));  // open: preset
  J_K_Flip_Flop j_k_ff_1 (
    .J(X), .K(X), .clk(clock_1_out), .Q(j_k_ff_1_q), .Qn(j_k_ff_1_qn), .reset(in_3));  // open: preset
  and and_1 (and_1_out, d_ff_1_qn, X);
  LED led_1 (.in(and_1_out));
  and and_2 (and_2_out, X, d_ff_1_q);
  LED led_2 (.in(and_2_out));
  and and_3 (and_3_out, X, j_k_ff_1_qn);
  LED led_3 (.in(and_3_out));
  and and_4 (and_4_out, j_k_ff_1_q, X);
  LED led_4 (.in(and_4_out));

  // Notes on the sheet:
  //   Z1
  //   Z2
  //   Z1
  //   Z2
endmodule
